// Logisim project IT012_LAB02_25520317.circ as structural Verilog: 9 circuits, main circuit FA2
module FA2 (
  input  A,
  input  B,
  input  Cin,
  output S,
  output Cout
);

  wire and_1_out, and_2_out, xor_1_out;

  xor xor_1 (xor_1_out, A, B);
  xor xor_2 (S, xor_1_out, Cin);
  and and_1 (and_1_out, A, B);
  and and_2 (and_2_out, Cin, xor_1_out);
  or or_1 (Cout, and_1_out, and_2_out);
endmodule

module ADDSUB4 (
  input  in_1,
  input  [3:0] A,
  input  [3:0] B,
  output [3:0] S
);

  wire FA2_2_cout, FA2_3_cout, FA2_cout;

  FA2 FA2 (.A(A[0]), .B(B[0]), .Cin(in_1), .S(S[0]), .Cout(FA2_cout));
  FA2 FA2_2 (.A(A[1]), .B(B[1]), .Cin(FA2_cout), .S(S[1]), .Cout(FA2_2_cout));
  FA2 FA2_3 (.A(A[2]), .B(B[2]), .Cin(FA2_2_cout), .S(S[2]), .Cout(FA2_3_cout));
  FA2 FA2_4 (.A(A[3]), .B(B[3]), .Cin(FA2_3_cout), .S(S[3]));  // open: Cout
endmodule

module ThiNghiem1 (
  input  SUB,
  input  [3:0] A,
  input  [3:0] B,
  output [3:0] S,
  output Cout
);

  wire FA2_2_cout, FA2_3_cout, FA2_cout, xor_1_out, xor_2_out, xor_3_out, xor_4_out;

  xor xor_1 (xor_1_out, SUB, B[0]);
  xor xor_2 (xor_2_out, SUB, B[1]);
  xor xor_3 (xor_3_out, SUB, B[2]);
  xor xor_4 (xor_4_out, SUB, B[3]);
  FA2 FA2 (.A(A[0]), .B(xor_1_out), .Cin(SUB), .S(S[0]), .Cout(FA2_cout));
  FA2 FA2_2 (.A(A[1]), .B(xor_2_out), .Cin(FA2_cout), .S(S[1]), .Cout(FA2_2_cout));
  FA2 FA2_3 (.A(A[2]), .B(xor_3_out), .Cin(FA2_2_cout), .S(S[2]), .Cout(FA2_3_cout));
  FA2 FA2_4 (.A(A[3]), .B(xor_4_out), .Cin(FA2_3_cout), .S(S[3]), .Cout(Cout));
endmodule

module ThiNghiem2 (
  input  [7:0] A,
  input  [7:0] B,
  input  [2:0] OP,
  output [7:0] AU,
  output Z,
  output [7:0] R,
  output [7:0] LU
);

  wire [7:0] adder_1_out, adder_2_out, and_1_out, not_1_out, or_1_out, subtractor_1_out, subtractor_2_out,
       xor_1_out;

  Adder adder_1 (.a(A), .b(B), .out(adder_1_out));  // open: cin, cout
  Adder adder_2 (.a(A), .b(8'h1), .out(adder_2_out));  // open: cin, cout
  Subtractor subtractor_1 (.a(A), .b(B), .out(subtractor_1_out));  // open: bin, bout
  Subtractor subtractor_2 (.a(A), .b(8'h1), .out(subtractor_2_out));  // open: bin, bout
  assign not_1_out = ~A;  // NOT_Gate not_1, 8 bits wide
  assign and_1_out = A & B;  // AND_Gate and_1, 8 bits wide
  assign or_1_out = A | B;  // OR_Gate or_1, 8 bits wide
  assign xor_1_out = A ^ B;  // XOR_Gate xor_1, 8 bits wide
  Multiplexer #(.select(2), .width(8), .enable("false")) multiplexer_1 (
    .in0(adder_1_out), .in1(adder_2_out), .in2(subtractor_1_out), .in3(subtractor_2_out), .out(AU),
    .sel(OP[1:0]));
  Multiplexer #(.select(2), .width(8), .enable("false")) multiplexer_2 (
    .in0(and_1_out), .in1(or_1_out), .in2(not_1_out), .in3(xor_1_out), .out(LU), .sel(OP[1:0]));
  Multiplexer #(.width(8), .enable("false")) multiplexer_3 (.in0(AU), .in1(LU), .out(R), .sel(OP[2]));
  nor nor_1 (Z, R[0], R[1], R[2], R[3], R[4], R[5], R[6], R[7]);
endmodule

module ThiNgiem3 (
  input  D,
  input  CLK,
  output Q1,
  output Q2,
  output Q3
);

  DLatch dlatch_1 (.D(D), .E(CLK), .Q(Q1));
  D_Flip_Flop d_ff_1 (.clk(CLK), .D(D), .Q(Q2));  // open: Qn, preset, en, reset
  DFF_MS dff_ms_1 (.D(D), .CLK(CLK), .Q(Q3));
endmodule

module DLatch (
  input  D,
  input  E,
  output Q
);

  Multiplexer #(.enable("false")) multiplexer_1 (.in0(Q), .in1(D), .out(Q), .sel(E));
endmodule

module DFF_MS (
  input  D,
  input  CLK,
  output Q
);

  wire dlatch_1_q, not_1_out;

  not not_1 (not_1_out, CLK);
  DLatch dlatch_1 (.D(D), .E(not_1_out), .Q(dlatch_1_q));
  DLatch dlatch_2 (.D(dlatch_1_q), .E(CLK), .Q(Q));
endmodule

// Q
module ReGFILE (
  input  WE,
  input  [1:0] RD,
  input  [1:0] RA,
  input  [7:0] DIN,
  input  CLK,
  input  [1:0] RB,
  output [7:0] R0,
  output [7:0] R1,
  output [7:0] R2,
  output [7:0] R3,
  output [7:0] QA,
  output [7:0] QB
);

  wire decoder_1_out0, decoder_1_out1, decoder_1_out2, decoder_1_out3;

  Decoder #(.select(2)) decoder_1 (
    .out0(decoder_1_out0), .out1(decoder_1_out1), .out2(decoder_1_out2), .out3(decoder_1_out3), .sel(RD),
    .en(WE));
  Register register_1 (.D(DIN), .en(decoder_1_out0), .Q(R0), .clk(CLK));  // open: clr
  Register register_2 (.D(DIN), .en(decoder_1_out1), .Q(R1), .clk(CLK));  // open: clr
  Register register_3 (.D(DIN), .en(decoder_1_out2), .Q(R2), .clk(CLK));  // open: clr
  Register register_4 (.D(DIN), .en(decoder_1_out3), .Q(R3), .clk(CLK));  // open: clr
  Multiplexer #(.select(2), .width(8), .enable("false")) multiplexer_1 (
    .in0(R0), .in1(R1), .in2(R2), .in3(R3), .out(QA), .sel(RA));
  Multiplexer #(.select(2), .width(8), .enable("false")) multiplexer_2 (
    .in0(R0), .in1(R1), .in2(R2), .in3(R3), .out(QB), .sel(RB));
endmodule

module ThiNghiem4 (
  input  [7:0] R,
  input  [1:0] RA,
  input  [1:0] RD,
  input  WE,
  input  [2:0] OP,
  input  [7:0] IMM,
  input  [1:0] RB,
  input  SRC,
  input  CLK,
  output [7:0] R0,
  output Z,
  output [7:0] R1,
  output [7:0] R2,
  output [7:0] R3
);

  wire undriven, undriven_4, undriven_5;
  wire [1:0] undriven_2, undriven_3, undriven_6;
  wire [7:0] multiplexer_1_out, regfile_1_qa, regfile_1_qb, thinghiem2_1_r;

  ThiNghiem2 thinghiem2_1 (.A(regfile_1_qa), .B(regfile_1_qb), .OP(OP), .R(thinghiem2_1_r), .LU(R));  // open: AU, Z
  Multiplexer #(.width(8), .enable("false")) multiplexer_1 (
    .in0(R), .in1(IMM), .out(multiplexer_1_out), .sel(undriven));
  ReGFILE regfile_1 (
    .WE(undriven_5), .RD(undriven_3), .RA(undriven_2), .DIN(multiplexer_1_out), .CLK(undriven_4),
    .RB(undriven_6), .R0(R1), .R1(R0), .R2(R2), .R3(R3), .QA(regfile_1_qa), .QB(regfile_1_qb));
endmodule
